# Fritzing sketch PlusHomefzz (saved by Fritzing 0.9.3b)
circuit board: 4.5cm x 8.5cm
breadboards: 1

parts:
  HLK-PM1 = HLK-PM01
  IC1 = Voltage Regulator AMS1117 [package=sot223]
  Boreal_Networks = ESP-WROOM-32 [ESP-32S] Module [part_number=ESP-WROOM-32]  # not connected
  part = screw terminal, 9 pins
  RELAY_5V2 = OMRON PCB Power Relay – G5LE [part_number="G5LE-1\n" package=THT]
  RELAY_5V1 = OMRON PCB Power Relay – G5LE [part_number="G5LE-1\n" package=THT]
  RELAY_5V3 = OMRON PCB Power Relay – G5LE [part_number="G5LE-1\n" package=THT]
  CAP = Tantalum Capacitor [capacitance="1 μF" voltage=16V package="D 7343 [SMD, tantalum]"]
  P___U = female pin header, 3 pins [form="♀ (female)"]  # not connected
  D1 = Rectifier Diode [part_number=1N4007 package="300 mil [THT]"]
  D2 = Rectifier Diode [part_number=1N4007 package="300 mil [THT]"]
  D3 = Rectifier Diode [part_number=1N4007 package="300 mil [THT]"]
  UP = TRANSISTOR_NPN [package=to-92-ammo]
  DOWN = TRANSISTOR_NPN [package=to-92-ammo]
  MID = TRANSISTOR_NPN [package=to-92-ammo]

nets:
  N1: HLK-PM1.AC#0, part.pin7, part.pin8
  N2: HLK-PM1.AC#1, part.pin9
  N3: HLK-PM1.-Vo, UP.E, DOWN.E, MID.E
  N4: HLK-PM1.+Vo, IC1.IN, RELAY_5V2.COIL1, RELAY_5V1.COIL2, RELAY_5V3.COIL1, D1.cathode, D2.cathode, D3.cathode
  N5: IC1.OUT, CAP.+
  N6: RELAY_5V2.COIL2, D2.anode, MID.C
  N7: RELAY_5V1.COIL1, D3.anode, DOWN.C
  N8: RELAY_5V3.COIL2, D1.anode, UP.C

notes:
  AC/N
  AC / L
  CON1
  CON2
  SWEC

custom parts:
  HLK-PM01: AC-DC 220V to 5V 5W Step-Down Power Supply Module
  ESP-WROOM-32 [ESP-32S] Module: Modulo personalizado, ESP32-S
